# Fritzing sketch Untitled Sketch (saved by Fritzing 0.9.3b)
circuit board: 8.24507cm x 5.23181cm
breadboards: 1

parts:
  IC1 = MICROCONTROLLER [package=dil28-3-zif_socket]
  LED1 = LED - 3mm [color="Red (633nm)" package="3 mm [THT]"]
  R1 = Resistor [tolerance=±5% resistance=220 package=THT]
  S1 = Pushbutton [package="[THT]"]
  VCC1 = 4 x AAA Battery Mount

nets:
  N1: IC1.VCC, VCC1.+
  N2: IC1.GND, LED1.cathode, S1.Pin_1, S1.Pin_2, VCC1.-
  N3: IC1.PB0(ICP), S1.Pin_3, S1.Pin_4
  N4: IC1.PB1(OC1A), R1.Pin_0
  N5: LED1.anode, R1.Pin_1

notes:
  Blink LED
  https://www.linkedin.com/in/saeedghorbani
